// Logisim project LogicMotorShortCircuitSecure.circ as structural Verilog: 1 circuit, main circuit main
module main (
  input  in_1,
  input  in_2
);

  wire IN1_minus, IN2_minus, nand_3_out, nand_4_out, OUT1, OUT2;

  nand nand_1 (IN1_minus, in_1, in_1);
  nand nand_2 (IN2_minus, in_2, in_2);
  LED led_1 (.in(OUT1));
  LED led_2 (.in(OUT2));
  nand nand_3 (nand_3_out, in_1, IN2_minus);
  nand nand_4 (nand_4_out, IN1_minus, in_2);
  nand nand_5 (OUT1, nand_3_out, nand_3_out);
  nand nand_6 (OUT2, nand_4_out, nand_4_out);

  // Other names for the same wires on the sheet: IN1 = in_1; IN2 = in_2
endmodule
